// Logisim project ETFStudent.circ as structural Verilog: 18 circuits, main circuit REG32_LD
module REG32_LD (
  input  [31:0] I15__0,
  input  LD,
  input  mr,
  input  CLK,
  output [31:0] A15__0
);

  // REG16_LD reg16_ld_1: pin names not known; wires that end beside it: CLK, mr, I15__0[31:16], A15__0[31:16], LD
  // REG16_LD reg16_ld_2: pin names not known; wires that end beside it: CLK, mr, I15__0[15:0], A15__0[15:0], LD

  // Notes on the sheet:
  //   __
endmodule

module KMADR (
  input  immed,
  input  memdir,
  input  regdir,
  input  regindpom,
  output [3:0] Adr3__0
);

  assign Adr3__0 = immed ? 4'b0010 : 4'bz;  // Controlled_Buffer controlled_buffer_1
  assign Adr3__0 = memdir ? 4'b0100 : 4'bz;  // Controlled_Buffer controlled_buffer_2
  assign Adr3__0 = regdir ? 4'b0101 : 4'bz;  // Controlled_Buffer controlled_buffer_3
  assign Adr3__0 = regindpom ? 4'b0111 : 4'bz;  // Controlled_Buffer controlled_buffer_4
endmodule

module KMOPR (
  input  LD,
  input  ST,
  input  ADD,
  input  SUB,
  input  BLSS,
  input  JLEQ,
  input  JMP,
  input  JSR,
  input  RTS,
  input  RTI,
  input  HALT,
  output [5:0] Adr5__0
);

  assign Adr5__0 = LD ? 6'b000010 : 6'bz;  // Controlled_Buffer controlled_buffer_1
  assign Adr5__0 = ST ? 6'b000100 : 6'bz;  // Controlled_Buffer controlled_buffer_2
  assign Adr5__0 = ADD ? 6'b001010 : 6'bz;  // Controlled_Buffer controlled_buffer_3
  assign Adr5__0 = SUB ? 6'b001100 : 6'bz;  // Controlled_Buffer controlled_buffer_4
  assign Adr5__0 = BLSS ? 6'b001110 : 6'bz;  // Controlled_Buffer controlled_buffer_5
  assign Adr5__0 = JLEQ ? 6'b010000 : 6'bz;  // Controlled_Buffer controlled_buffer_6
  assign Adr5__0 = JMP ? 6'b010001 : 6'bz;  // Controlled_Buffer controlled_buffer_7
  assign Adr5__0 = JSR ? 6'b010010 : 6'bz;  // Controlled_Buffer controlled_buffer_8
  assign Adr5__0 = RTS ? 6'b010111 : 6'bz;  // Controlled_Buffer controlled_buffer_9
  assign Adr5__0 = RTI ? 6'b011110 : 6'bz;  // Controlled_Buffer controlled_buffer_10
  assign Adr5__0 = HALT ? 6'b100010 : 6'bz;  // Controlled_Buffer controlled_buffer_11
endmodule

module REG6_INC_LD (
  input  [5:0] I5__0,
  input  LD,
  input  INC,
  input  mr,
  input  CLK,
  output [5:0] A5__0
);

  wire reg2m_inc_ld_1_p7, reg2m_inc_ld_2_p8;

  // REG2m_INC_LD reg2m_inc_ld_1: pin names not known; wires that end beside it: CLK, mr, I5__0[5:4], A5__0[5:4], LD, INC, reg2m_inc_ld_1_p7
  // REG2m_INC_LD reg2m_inc_ld_2: pin names not known; wires that end beside it: CLK, reg2m_inc_ld_1_p7, mr, I5__0[3:2], A5__0[3:2], LD, INC, reg2m_inc_ld_2_p8
  // REG2m_INC_LD reg2m_inc_ld_3: pin names not known; wires that end beside it: CLK, reg2m_inc_ld_2_p8, mr, I5__0[1:0], A5__0[1:0], LD, INC, INC

  // Notes on the sheet:
  //   __
endmodule

module REG5_INC_LD (
  input  [4:0] I4__0,
  input  LD,
  input  INC,
  input  mr,
  input  CLK,
  output [4:0] A4__0
);

  wire reg4m_inc_ld_1_p7;

  // REG4m_INC_LD reg4m_inc_ld_1: pin names not known; wires that end beside it: CLK, mr, I4__0[4:1], A4__0[4:1], LD, INC, reg4m_inc_ld_1_p7
  // REG1m_INC_LD reg1m_inc_ld_1: pin names not known; wires that end beside it: CLK, reg4m_inc_ld_1_p7, mr, I4__0[0], A4__0[0], LD, INC, INC

  // Notes on the sheet:
  //   __
endmodule

module ROM32x20 (
  input  [4:0] A4__0,
  input  CS,
  output [19:0] DOUT19__0
);

  ROM #(.addrWidth(5), .dataWidth(20)) rom_1 (.addr(A4__0), .data(DOUT19__0), .sel(CS));
endmodule

module GPR16x16 (
  input  [15:0] DI15__0,
  input  [3:0] A3__0,
  input  WR,
  input  CLK,
  output [15:0] DO15__0
);

  wire and_5_out, and_6_out, and_7_out, and_8_out, CS0, CS1, CS2, CS3, CS4, CS5, CS6, CS7, CS8, CS9, CS10,
       CS11, CS12, CS13, CS14, CS15, reg16_ld_1_p4, reg16_ld_2_p4, reg16_ld_3_p4, reg16_ld_4_p4,
       reg16_ld_9_p4, reg16_ld_10_p4, reg16_ld_11_p4, reg16_ld_12_p4, reg16_ld_13_p4, reg16_ld_14_p4,
       reg16_ld_15_p4, reg16_ld_16_p4;
  wire [15:0] reg16_ld_1_p3, reg16_ld_2_p3, reg16_ld_3_p3, reg16_ld_4_p3, reg16_ld_5_p3, reg16_ld_6_p3,
       reg16_ld_7_p3, reg16_ld_8_p3, reg16_ld_9_p3, reg16_ld_10_p3, reg16_ld_11_p3, reg16_ld_12_p3,
       reg16_ld_13_p3, reg16_ld_14_p3, reg16_ld_15_p3, reg16_ld_16_p3;

  // DC4_16 dc4_16_1: pin names not known; wires that end beside it: A3__0, 1'b1, CS0, CS1, CS2, CS3, CS4, CS5, CS6, CS7, CS8, CS9, CS10, CS11, CS12, CS13, CS14, CS15
  // REG16_LD reg16_ld_1: pin names not known; wires that end beside it: CLK, DI15__0, reg16_ld_1_p3, reg16_ld_1_p4
  assign DO15__0 = CS0 ? reg16_ld_1_p3 : 16'bz;  // Controlled_Buffer controlled_buffer_1
  // REG16_LD reg16_ld_2: pin names not known; wires that end beside it: CLK, DI15__0, reg16_ld_2_p3, reg16_ld_2_p4
  assign DO15__0 = CS4 ? reg16_ld_2_p3 : 16'bz;  // Controlled_Buffer controlled_buffer_2
  // REG16_LD reg16_ld_3: pin names not known; wires that end beside it: CLK, DI15__0, reg16_ld_3_p3, reg16_ld_3_p4
  assign DO15__0 = CS8 ? reg16_ld_3_p3 : 16'bz;  // Controlled_Buffer controlled_buffer_3
  // REG16_LD reg16_ld_4: pin names not known; wires that end beside it: CLK, DI15__0, reg16_ld_4_p3, reg16_ld_4_p4
  assign DO15__0 = CS12 ? reg16_ld_4_p3 : 16'bz;  // Controlled_Buffer controlled_buffer_4
  and and_1 (reg16_ld_1_p4, WR, CS0);
  and and_2 (reg16_ld_2_p4, WR, CS4);
  and and_3 (reg16_ld_3_p4, WR, CS8);
  and and_4 (reg16_ld_4_p4, WR, CS12);
  and and_5 (and_5_out, WR, CS1);
  // REG16_LD reg16_ld_5: pin names not known; wires that end beside it: CLK, DI15__0, reg16_ld_5_p3, and_5_out
  assign DO15__0 = CS1 ? reg16_ld_5_p3 : 16'bz;  // Controlled_Buffer controlled_buffer_5
  and and_6 (and_6_out, WR, CS5);
  // REG16_LD reg16_ld_6: pin names not known; wires that end beside it: CLK, DI15__0, reg16_ld_6_p3, and_6_out
  assign DO15__0 = CS5 ? reg16_ld_6_p3 : 16'bz;  // Controlled_Buffer controlled_buffer_6
  and and_7 (and_7_out, WR, CS9);
  // REG16_LD reg16_ld_7: pin names not known; wires that end beside it: CLK, DI15__0, reg16_ld_7_p3, and_7_out
  assign DO15__0 = CS9 ? reg16_ld_7_p3 : 16'bz;  // Controlled_Buffer controlled_buffer_7
  and and_8 (and_8_out, WR, CS13);
  // REG16_LD reg16_ld_8: pin names not known; wires that end beside it: CLK, DI15__0, reg16_ld_8_p3, and_8_out
  assign DO15__0 = CS13 ? reg16_ld_8_p3 : 16'bz;  // Controlled_Buffer controlled_buffer_8
  // REG16_LD reg16_ld_9: pin names not known; wires that end beside it: CLK, DI15__0, reg16_ld_9_p3, reg16_ld_9_p4
  assign DO15__0 = CS2 ? reg16_ld_9_p3 : 16'bz;  // Controlled_Buffer controlled_buffer_9
  // REG16_LD reg16_ld_10: pin names not known; wires that end beside it: CLK, DI15__0, reg16_ld_10_p3, reg16_ld_10_p4
  assign DO15__0 = CS6 ? reg16_ld_10_p3 : 16'bz;  // Controlled_Buffer controlled_buffer_10
  // REG16_LD reg16_ld_11: pin names not known; wires that end beside it: CLK, DI15__0, reg16_ld_11_p3, reg16_ld_11_p4
  assign DO15__0 = CS10 ? reg16_ld_11_p3 : 16'bz;  // Controlled_Buffer controlled_buffer_11
  // REG16_LD reg16_ld_12: pin names not known; wires that end beside it: CLK, DI15__0, reg16_ld_12_p3, reg16_ld_12_p4
  assign DO15__0 = CS14 ? reg16_ld_12_p3 : 16'bz;  // Controlled_Buffer controlled_buffer_12
  and and_9 (reg16_ld_9_p4, WR, CS2);
  and and_10 (reg16_ld_10_p4, WR, CS6);
  and and_11 (reg16_ld_11_p4, WR, CS10);
  and and_12 (reg16_ld_12_p4, WR, CS14);
  // REG16_LD reg16_ld_13: pin names not known; wires that end beside it: CLK, DI15__0, reg16_ld_13_p3, reg16_ld_13_p4
  assign DO15__0 = CS3 ? reg16_ld_13_p3 : 16'bz;  // Controlled_Buffer controlled_buffer_13
  // REG16_LD reg16_ld_14: pin names not known; wires that end beside it: CLK, DI15__0, reg16_ld_14_p3, reg16_ld_14_p4
  assign DO15__0 = CS7 ? reg16_ld_14_p3 : 16'bz;  // Controlled_Buffer controlled_buffer_14
  // REG16_LD reg16_ld_15: pin names not known; wires that end beside it: CLK, DI15__0, reg16_ld_15_p3, reg16_ld_15_p4
  assign DO15__0 = CS11 ? reg16_ld_15_p3 : 16'bz;  // Controlled_Buffer controlled_buffer_15
  // REG16_LD reg16_ld_16: pin names not known; wires that end beside it: CLK, DI15__0, reg16_ld_16_p3, reg16_ld_16_p4
  assign DO15__0 = CS15 ? reg16_ld_16_p3 : 16'bz;  // Controlled_Buffer controlled_buffer_16
  and and_13 (reg16_ld_13_p4, WR, CS3);
  and and_14 (reg16_ld_14_p4, WR, CS7);
  and and_15 (reg16_ld_15_p4, WR, CS11);
  and and_16 (reg16_ld_16_p4, WR, CS15);

  // Other names for the same wires on the sheet: inREG[15:0] = DI15__0; outREG[15:0] = DO15__0
endmodule

module ROM32x26 (
  input  [4:0] A4__0,
  input  CS,
  output [25:0] DOUT23__0
);

  ROM #(.addrWidth(5), .dataWidth(26)) rom_1 (.addr(A4__0), .data(DOUT23__0), .sel(CS));
endmodule

module MP2_5b (
  input  En,
  input  [4:0] in_2,
  input  [4:0] in_3,
  input  S0,
  output [4:0] Y
);

  wire not_1_out;
  wire [4:0] and_1_out, and_2_out, bit_extender_1_out, bit_extender_2_out, bit_extender_3_out, or_1_out;

  Pull_Resistor #(.pull(1)) pull_resistor_1 (.node(En));
  assign bit_extender_1_out = {{4{S0}}, S0};  // Bit_Extender bit_extender_1
  not not_1 (not_1_out, S0);
  assign bit_extender_2_out = {{4{not_1_out}}, not_1_out};  // Bit_Extender bit_extender_2
  assign and_1_out = in_2 & bit_extender_2_out;  // AND_Gate and_1, 5 bits wide
  assign and_2_out = in_3 & bit_extender_1_out;  // AND_Gate and_2, 5 bits wide
  assign bit_extender_3_out = {{4{En}}, En};  // Bit_Extender bit_extender_3
  assign or_1_out = and_1_out | and_2_out;  // OR_Gate or_1, 5 bits wide
  assign Y = bit_extender_3_out & or_1_out;  // AND_Gate and_3, 5 bits wide

  // Notes on the sheet:
  //   I0
  //   4..0
  //   I1
  //   4..0
  //   Ako En nije priključen (stanje visoke impednase - HiZ),
  //   uezti za podrazumevanu vrednost logičku jedinicu
  //   4..0
endmodule

module KMADR7 (
  input  immed,
  input  memdir,
  input  memind,
  input  regind,
  input  postincr,
  input  postdec,
  input  regdir,
  output [4:0] Adr4__0
);

  assign Adr4__0 = immed ? 5'b00010 : 5'bz;  // Controlled_Buffer controlled_buffer_1
  assign Adr4__0 = memdir ? 5'b00011 : 5'bz;  // Controlled_Buffer controlled_buffer_2
  assign Adr4__0 = memind ? 5'b00100 : 5'bz;  // Controlled_Buffer controlled_buffer_3
  assign Adr4__0 = regind ? 5'b01010 : 5'bz;  // Controlled_Buffer controlled_buffer_4
  assign Adr4__0 = postincr ? 5'b01011 : 5'bz;  // Controlled_Buffer controlled_buffer_5
  assign Adr4__0 = postdec ? 5'b01111 : 5'bz;  // Controlled_Buffer controlled_buffer_6
  assign Adr4__0 = regdir ? 5'b10011 : 5'bz;  // Controlled_Buffer controlled_buffer_7
endmodule

module REG16_CL_INC_LD (
  input  [15:0] I15__0,
  input  LD,
  input  CL,
  input  INC,
  input  mr,
  input  CLK,
  output [15:0] out_7
);

  wire reg4m_cl_inc_ld_1_p8, reg4m_cl_inc_ld_2_p9, reg4m_cl_inc_ld_3_p9;

  // REG4m_CL_INC_LD reg4m_cl_inc_ld_1: pin names not known; wires that end beside it: CL, CLK, mr, I15__0[15:12], out_7[15:12], LD, mr, reg4m_cl_inc_ld_1_p8
  // REG4m_CL_INC_LD reg4m_cl_inc_ld_2: pin names not known; wires that end beside it: CL, CLK, reg4m_cl_inc_ld_1_p8, mr, I15__0[11:8], out_7[11:8], LD, mr, reg4m_cl_inc_ld_2_p9
  // REG4m_CL_INC_LD reg4m_cl_inc_ld_3: pin names not known; wires that end beside it: CL, CLK, reg4m_cl_inc_ld_2_p9, mr, I15__0[7:4], out_7[7:4], LD, mr, reg4m_cl_inc_ld_3_p9
  // REG4m_CL_INC_LD reg4m_cl_inc_ld_4: pin names not known; wires that end beside it: CL, CLK, reg4m_cl_inc_ld_3_p9, mr, I15__0[3:0], out_7[3:0], LD, INC, INC

  // Notes on the sheet:
  //   __
endmodule

module ALU16_ADD_INC_OR (
  input  [15:0] A15__0,
  input  [15:0] B15__0,
  input  add,
  input  inc,
  input  \or ,
  output [15:0] DOUT15__0,
  output Cout
);

  wire add16_1_p1, add16_2_p1;
  wire [15:0] add16_1_p3, add16_2_p3, or_1_out;

  // ADD16 add16_1: pin names not known; wires that end beside it: add16_1_p1, A15__0, add16_1_p3, B15__0, 1'b0
  // ADD16 add16_2: pin names not known; wires that end beside it: add16_2_p1, B15__0, add16_2_p3, {16{1'b0}}, 1'b1
  assign or_1_out = B15__0 | A15__0;  // OR_Gate or_1, 16 bits wide
  assign Cout = add ? add16_2_p1 : 1'bz;  // Controlled_Buffer controlled_buffer_1
  assign Cout = inc ? add16_1_p1 : 1'bz;  // Controlled_Buffer controlled_buffer_2
  assign Cout = \or  ? 1'b0 : 1'bz;  // Controlled_Buffer controlled_buffer_3
  assign DOUT15__0 = add ? add16_1_p3 : 16'bz;  // Controlled_Buffer controlled_buffer_4
  assign DOUT15__0 = inc ? add16_2_p3 : 16'bz;  // Controlled_Buffer controlled_buffer_5
  assign DOUT15__0 = \or  ? or_1_out : 16'bz;  // Controlled_Buffer controlled_buffer_6
endmodule

module KMOPR20 (
  input  [19:0] inst19__0,
  output [6:0] Adr6__0
);

  assign Adr6__0 = inst19__0[0] ? 7'b0000010 : 7'bz;  // Controlled_Buffer controlled_buffer_1
  assign Adr6__0 = inst19__0[1] ? 7'b0000011 : 7'bz;  // Controlled_Buffer controlled_buffer_2
  assign Adr6__0 = inst19__0[2] ? 7'b0001010 : 7'bz;  // Controlled_Buffer controlled_buffer_3
  assign Adr6__0 = inst19__0[3] ? 7'b0010110 : 7'bz;  // Controlled_Buffer controlled_buffer_4
  assign Adr6__0 = inst19__0[4] ? 7'b0011000 : 7'bz;  // Controlled_Buffer controlled_buffer_5
  assign Adr6__0 = inst19__0[5] ? 7'b0011010 : 7'bz;  // Controlled_Buffer controlled_buffer_6
  assign Adr6__0 = inst19__0[6] ? 7'b0011111 : 7'bz;  // Controlled_Buffer controlled_buffer_7
  assign Adr6__0 = inst19__0[7] ? 7'b0100111 : 7'bz;  // Controlled_Buffer controlled_buffer_8
  assign Adr6__0 = inst19__0[8] ? 7'b0101001 : 7'bz;  // Controlled_Buffer controlled_buffer_9
  assign Adr6__0 = inst19__0[9] ? 7'b0100111 : 7'bz;  // Controlled_Buffer controlled_buffer_10
  assign Adr6__0 = inst19__0[11] ? 7'b0101011 : 7'bz;  // Controlled_Buffer controlled_buffer_11
  assign Adr6__0 = inst19__0[10] ? 7'b0100111 : 7'bz;  // Controlled_Buffer controlled_buffer_12
  assign Adr6__0 = inst19__0[12] ? 7'b0101101 : 7'bz;  // Controlled_Buffer controlled_buffer_13
  assign Adr6__0 = inst19__0[13] ? 7'b0101110 : 7'bz;  // Controlled_Buffer controlled_buffer_14
  assign Adr6__0 = inst19__0[14] ? 7'b0110011 : 7'bz;  // Controlled_Buffer controlled_buffer_15
  assign Adr6__0 = inst19__0[15] ? 7'b0110101 : 7'bz;  // Controlled_Buffer controlled_buffer_16
  assign Adr6__0 = inst19__0[16] ? 7'b0111100 : 7'bz;  // Controlled_Buffer controlled_buffer_17
  assign Adr6__0 = inst19__0[17] ? 7'b0111110 : 7'bz;  // Controlled_Buffer controlled_buffer_18
  assign Adr6__0 = inst19__0[18] ? 7'b1000000 : 7'bz;  // Controlled_Buffer controlled_buffer_19
  assign Adr6__0 = inst19__0[19] ? 7'b1000010 : 7'bz;  // Controlled_Buffer controlled_buffer_20

  // Other names for the same wires on the sheet: HALT = inst19__0[0]; RTS = inst19__0[1]; RTI = inst19__0[2];
  //   ROR = inst19__0[3]; RORC = inst19__0[4]; PUSH = inst19__0[5]; POP = inst19__0[6]; BLEQ = inst19__0[7];
  //   BGREU = inst19__0[8]; BNNG = inst19__0[9]; BGRT = inst19__0[10]; JLEQ = inst19__0[11]; JMP = inst19__0[12];
  //   JSR = inst19__0[13]; LD = inst19__0[14]; ST = inst19__0[15]; ADD = inst19__0[16]; INC = inst19__0[17];
  //   OR = inst19__0[18]; STRFIND = inst19__0[19]
endmodule

module MP2_7b (
  input  En,
  input  [6:0] in_2,
  input  [6:0] in_3,
  input  S0,
  output [6:0] out_5
);

  wire not_1_out;
  wire [6:0] and_1_out, and_2_out, bit_extender_1_out, bit_extender_2_out, bit_extender_3_out, or_1_out;

  Pull_Resistor #(.pull(1)) pull_resistor_1 (.node(En));
  assign bit_extender_1_out = {{6{S0}}, S0};  // Bit_Extender bit_extender_1
  not not_1 (not_1_out, S0);
  assign bit_extender_2_out = {{6{not_1_out}}, not_1_out};  // Bit_Extender bit_extender_2
  assign and_1_out = in_2 & bit_extender_2_out;  // AND_Gate and_1, 7 bits wide
  assign and_2_out = in_3 & bit_extender_1_out;  // AND_Gate and_2, 7 bits wide
  assign bit_extender_3_out = {{6{En}}, En};  // Bit_Extender bit_extender_3
  assign or_1_out = and_1_out | and_2_out;  // OR_Gate or_1, 7 bits wide
  assign out_5 = bit_extender_3_out & or_1_out;  // AND_Gate and_3, 7 bits wide

  // Notes on the sheet:
  //   I0
  //   6..0
  //   I1
  //   6..0
  //   Ako En nije priključen (stanje visoke impednase - HiZ),
  //   uezti za podrazumevanu vrednost logičku jedinicu
  //   Y
  //   6..0
endmodule

module REG7_INC_LD (
  input  [6:0] I6__0,
  input  LD,
  input  INC,
  input  mr,
  input  CLK,
  output [6:0] A6__0
);

  wire reg1_inc_ld_1_p6, reg2m_inc_ld_1_p8;

  // REG1_INC_LD reg1_inc_ld_1: pin names not known; wires that end beside it: CLK, mr, I6__0[6], A6__0[6], LD, reg1_inc_ld_1_p6
  // REG2m_INC_LD reg2m_inc_ld_1: pin names not known; wires that end beside it: CLK, reg1_inc_ld_1_p6, mr, I6__0[5:4], A6__0[5:4], LD, INC, reg2m_inc_ld_1_p8
  // REG4m_CL_INC_LD reg4m_cl_inc_ld_1: pin names not known; wires that end beside it: CLK, reg2m_inc_ld_1_p8, mr, I6__0[3:0], A6__0[3:0], LD, INC, INC

  // Notes on the sheet:
  //   __
endmodule

module ROM128x52 (
  input  [6:0] A6__0,
  input  CS,
  output [19:0] DOUT51__32,
  output [31:0] DOUT31__0
);

  ROM #(.addrWidth(7), .dataWidth(20)) rom_1 (.addr(A6__0), .data(DOUT51__32), .sel(CS));
  ROM #(.addrWidth(7), .dataWidth(32)) rom_2 (.addr(A6__0), .data(DOUT31__0), .sel(CS));
endmodule

module pCD4 (
  input  En,
  input  C3,
  input  C2,
  input  C1,
  input  C0,
  output Z1,
  output Z0,
  output W
);

  wire and_1_out, or_1_out, or_2_out, or_3_out;

  Pull_Resistor #(.pull(1)) pull_resistor_1 (.node(En));
  or or_1 (or_1_out, C3, C2, C1, C0);
  and and_1 (and_1_out, C1, ~C2);  // AND_Gate
  or or_2 (or_2_out, C3, C2);
  or or_3 (or_3_out, C3, and_1_out);
  and and_2 (Z1, En, or_2_out);
  and and_3 (Z0, or_3_out, En);
  and and_4 (W, En, or_1_out);

  // Notes on the sheet:
  //   uezti za podrazumevanu vrednost logičku jedinicu
  //   Ako En nije priključen (stanje visoke impednase - HiZ),
endmodule

module ROM32x26_2 (
  input  [4:0] A4__0,
  input  CS,
  output [25:0] DOUT23__0
);

  ROM #(.addrWidth(5), .dataWidth(26)) rom_1 (.addr(A4__0), .data(DOUT23__0), .sel(CS));
endmodule
