// Logisim project ORT2Project.circ as structural Verilog: 8 circuits, main circuit COMPUTER
module COMPUTER (
);

  wire BTN_RST_out, CLK, cpu_1_inta, interrupt_interface_4_1_p4, interrupt_interface_4_1_p5,
       interrupt_interface_4_1_p6, interrupt_interface_4_1_p7, pull_resistor_2_node, pull_resistor_5_node,
       ram_1_out_8, rst;
  wire [1:0] cpu_1_uext1__0;
  wire [3:0] interrupt_interface_4_1_p1;
  wire [7:0] pull_resistor_4_node, ram_1_out_7;
  wire [15:0] pull_resistor_3_node;

  Button BTN_RST (.out(BTN_RST_out));
  Clock u_CLK (.out(CLK));
  // RisingEdge risingedge_1: pin names not known; wires that end beside it: BTN_RST_out, CLK, rst
  RAM ram_1 (
    .in_1(pull_resistor_3_node), .in_2(CLK), .in_3(pull_resistor_4_node), .in_4(pull_resistor_2_node),
    .in_5(pull_resistor_5_node), .in_6(rst), .out_7(ram_1_out_7), .out_8(ram_1_out_8));
  Pull_Resistor pull_resistor_1 (.node(ram_1_out_7));
  Pull_Resistor pull_resistor_2 (.node(pull_resistor_2_node));
  Pull_Resistor pull_resistor_3 (.node(pull_resistor_3_node));
  Pull_Resistor pull_resistor_4 (.node(pull_resistor_4_node));
  Pull_Resistor pull_resistor_5 (.node(pull_resistor_5_node));
  Pull_Resistor pull_resistor_6 (.node(ram_1_out_8));
  CPU cpu_1 (
    .in_1(rst), .in_2(CLK), .in_3(ram_1_out_8), .in_4(ram_1_out_7), .ABUS(pull_resistor_3_node),
    .DOUTBUS(pull_resistor_4_node), .out_8(pull_resistor_2_node), .out_9(pull_resistor_5_node),
    .inta(cpu_1_inta), .intr3__0(interrupt_interface_4_1_p1), .UEXT1__0(cpu_1_uext1__0));
  // INTERRUPT_INTERFACE_4 interrupt_interface_4_1: pin names not known; wires that end beside it: interrupt_interface_4_1_p1, cpu_1_inta, cpu_1_uext1__0, interrupt_interface_4_1_p4, interrupt_interface_4_1_p5, interrupt_interface_4_1_p6, interrupt_interface_4_1_p7, CLK
  Button BTN_INTR3 (.out(interrupt_interface_4_1_p4));
  Button BTN_INTR2 (.out(interrupt_interface_4_1_p5));
  Button BTN_INTR1 (.out(interrupt_interface_4_1_p6));
  Button BTN_INTR0 (.out(interrupt_interface_4_1_p7));
endmodule

module CPU (
  input  in_1,
  input  in_2,
  input  in_3,
  input  [7:0] in_4,
  input  [3:0] intr3__0,
  output [15:0] ABUS,
  output [7:0] DOUTBUS,
  output out_8,
  output out_9,
  output inta,
  output [1:0] UEXT1__0
);

  wire C16;
  wire [3:0] common_1_phaseffbus;
  wire [6:0] common_1_addrbus, pull_resistor_2_node;
  wire [15:0] A, ALU, B, CNT, INTRADDR, PC, PSW;
  wire [19:0] common_1_instrucbus;
  wire [23:0] pull_resistor_5_node, pull_resistor_6_node, pull_resistor_7_node;
  wire [31:0] IR;

  COMMON common_1 (
    .CLK(in_2), .RST(in_1), .DIN(in_4), .CMEMBUS(pull_resistor_5_node), .MAR(ABUS), .MDR(DOUTBUS),
    .PHASEFFBUS(common_1_phaseffbus), .INSTRUCBUS(common_1_instrucbus), .ADDRBUS(common_1_addrbus),
    .PSW(PSW), .CREGBUS(pull_resistor_6_node), .CFFBUS(pull_resistor_7_node), .B(B),
    .CPSW(pull_resistor_2_node), .ALU(ALU), .IVTPPDSP(INTRADDR), .A(A), .CNT(CNT), .PC(PC), .IR(IR), .C16(C16));
  Pull_Resistor pull_resistor_1 (.node(common_1_phaseffbus));
  Pull_Resistor pull_resistor_2 (.node(pull_resistor_2_node));
  Pull_Resistor pull_resistor_3 (.node(common_1_instrucbus));
  Pull_Resistor pull_resistor_4 (.node(common_1_addrbus));
  Pull_Resistor pull_resistor_5 (.node(pull_resistor_5_node));
  Pull_Resistor pull_resistor_6 (.node(pull_resistor_6_node));
  Pull_Resistor pull_resistor_7 (.node(pull_resistor_7_node));
  FETCH fetch_1 (
    .in_1(in_1), .in_2(in_2), .in_3(in_3), .PHASEFFBUS(common_1_phaseffbus),
    .INSTRUCBUS(common_1_instrucbus), .ADDRBUS(common_1_addrbus), .PSW(PSW), .rdMEM(out_9),
    .CMEMBUS(pull_resistor_5_node), .CFFBUS(pull_resistor_7_node), .CREGBUS(pull_resistor_6_node));
  ADDR addr_1 (
    .in_1(in_1), .in_2(in_2), .in_3(in_3), .PHASEFFBUS(common_1_phaseffbus),
    .INSTRUCBUS(common_1_instrucbus), .ADDRBUS(common_1_addrbus), .rdMEM(out_9),
    .CMEMBUS(pull_resistor_5_node), .CFFBUS(pull_resistor_7_node), .CREGBUS(pull_resistor_6_node));
  EXEC exec_1 (
    .in_1(in_1), .in_2(in_2), .in_3(in_3), .B(B), .PHASEFFBUS(common_1_phaseffbus),
    .INSTRUCBUS(common_1_instrucbus), .ADDRBUS(common_1_addrbus), .PSW(PSW), .ALU(ALU),
    .CMEMBUS(pull_resistor_5_node), .CFFBUS(pull_resistor_7_node), .CREGBUS(pull_resistor_6_node),
    .CPSW(pull_resistor_2_node), .rdMEM(out_9), .wrMEM(out_8), .A(A), .CNT(CNT), .PC(PC), .IR(IR), .C16(C16),
    .MDR(DOUTBUS));
  INTR intr_1 (
    .in_1(in_1), .in_2(in_2), .in_3(in_3), .PHASEFFBUS(common_1_phaseffbus),
    .INSTRUCBUS(common_1_instrucbus), .PSW(PSW), .intr(intr3__0), .ADDIVTP(INTRADDR),
    .CMEMBUS(pull_resistor_5_node), .CFFBUS(pull_resistor_7_node), .CREGBUS(pull_resistor_6_node),
    .rdMEM(out_9), .wrMEM(out_8), .UEXT1__0(UEXT1__0), .inta(inta));
  Pull_Resistor pull_resistor_8 (.node(out_9));
  Pull_Resistor pull_resistor_9 (.node(out_8));

  // Other names for the same wires on the sheet: CLK = in_2; DIN7__0[7:0] = in_4; FCBUS = in_3; MAR[15:0] = ABUS;
  //   MDR[7:0] = DOUTBUS; RD = out_9; rst = in_1; WR = out_8
endmodule

module COMMON (
  input  CLK,
  input  RST,
  input  [7:0] DIN,
  input  [15:0] ALU,
  input  [15:0] CNT,
  input  C16,
  input  [15:0] IVTPPDSP,
  input  [23:0] CMEMBUS,
  input  [23:0] CFFBUS,
  input  [23:0] CREGBUS,
  input  [6:0] CPSW,
  output [15:0] MAR,
  output [7:0] MDR,
  output [15:0] A,
  output [15:0] PC,
  output [31:0] IR,
  output [3:0] PHASEFFBUS,
  output [19:0] INSTRUCBUS,
  output [6:0] ADDRBUS,
  output [15:0] PSW,
  output [15:0] B
);

  wire ADRINST, adrinst_t, and_1_out, and_2_out, and_5_out, and_6_out, and_7_out, and_11_out, and_12_out,
       and_13_out, and_14_out, and_15_out, and_16_out, and_17_out, and_18_out, and_19_out, and_20_out,
       and_21_out, and_22_out, and_23_out, and_24_out, and_25_out, and_26_out, and_27_out, and_28_out,
       and_29_out, and_30_out, and_31_out, and_32_out, and_33_out, and_34_out, bezadrinst, branchinst,
       dc3_8_4_p3, dc3_8_4_p4, dc3_8_4_p5, doDEC, doINC, jmpinst, mp2_1b_1_p3, mp2_8b_1_p3, mp2_8b_2_p3,
       mp4_16b_1_p5, mp4_16b_2_p6, mp8_8b_1_p8, mp8_16b_1_p8, mp8_16b_2_p8, nor_1_out, nor_2_out, not_1_out,
       not_4_out, not_5_out, or_2_out, or_3_out, or_4_out, or_5_out, or_6_out, or_7_out, or_8_out, or_9_out,
       reg16_inc_ld_2_p4, rsff_2_p4, rsff_3_p4, rsff_6_p4, rsff_7_p4, rsff_8_p3, rsff_8_p4, rsff_9_p4,
       rsff_10_p4;
  wire [7:0] GPR7__0;
  wire [15:0] DW, mp2_16b_1_p3, SP15__0;
  wire [15:8] GPR15__0;

  // MP2_8b mp2_8b_1: pin names not known; wires that end beside it: CREGBUS[7], MDR, mp2_8b_1_p3, GPR15__0, 1'b1
  // REG8 reg8_1: pin names not known; wires that end beside it: 1'b0, 1'b0, 1'b0, 1'b0, 1'b0, CLK, 1'b1, mp2_8b_1_p3, DW[15:8], CREGBUS[6], 1'b0, 1'b0, doINC, doDEC
  // MP8_16b mp8_16b_1: pin names not known; wires that end beside it: CMEMBUS[7], CMEMBUS[6], CMEMBUS[5], PC, IR[15:0], DW, {GPR15__0, GPR7__0}, mp8_16b_1_p8, SP15__0, B, IVTPPDSP, 1'b1
  // REG16_INC_LD reg16_inc_ld_1: pin names not known; wires that end beside it: CLK, mp8_16b_1_p8, MAR, CMEMBUS[0], CMEMBUS[1]
  and and_1 (and_1_out, ~IR[27], ~IR[31], ~IR[30], PSW[0]);  // AND_Gate
  // DC2_4 dc2_4_1: pin names not known; wires that end beside it: IR[29:28], and_1_out, bezadrinst, branchinst, jmpinst, adrinst_t
  // DC3_8 dc3_8_1: pin names not known; wires that end beside it: IR[26:24], bezadrinst, INSTRUCBUS[0], INSTRUCBUS[1], INSTRUCBUS[2], INSTRUCBUS[3], INSTRUCBUS[4], INSTRUCBUS[5], INSTRUCBUS[6]
  // DC3_8 dc3_8_2: pin names not known; wires that end beside it: IR[26:24], branchinst, INSTRUCBUS[7], INSTRUCBUS[8], INSTRUCBUS[9], INSTRUCBUS[10], INSTRUCBUS[11]
  // REG16 reg16_1: pin names not known; wires that end beside it: 1'b0, 1'b0, 1'b0, 1'b0, CLK, 1'b0, 1'b1, 16'hf000, SP15__0, RST, 1'b0, 1'b0, CREGBUS[14], CREGBUS[15]
  and and_2 (and_2_out, DW[0], DW[1], DW[2], DW[3], DW[4], DW[5], DW[6], DW[7]);
  nor nor_1 (nor_1_out, DW[0], DW[1], DW[2], DW[3], DW[4], DW[5], DW[6], DW[7]);
  // REG8_LD reg8_ld_1: pin names not known; wires that end beside it: CLK, MDR, IR[23:16], CREGBUS[2]
  // REG8_LD reg8_ld_2: pin names not known; wires that end beside it: CLK, MDR, IR[31:24], CREGBUS[3]
  and and_3 (doINC, CREGBUS[8], and_2_out);
  and and_4 (doDEC, CREGBUS[9], nor_1_out);
  and and_5 (and_5_out, ~IR[26], ~IR[25], jmpinst);  // AND_Gate
  // DC1_2 dc1_2_1: pin names not known; wires that end beside it: IR[24], and_5_out, INSTRUCBUS[12], INSTRUCBUS[13]
  // DC3_8 dc3_8_3: pin names not known; wires that end beside it: IR[26:24], adrinst_t, INSTRUCBUS[14], INSTRUCBUS[15], INSTRUCBUS[16], INSTRUCBUS[17], INSTRUCBUS[18], INSTRUCBUS[19]
  // MP2_8b mp2_8b_2: pin names not known; wires that end beside it: CREGBUS[5], MDR, mp2_8b_2_p3, GPR7__0, 1'b1
  // REG8 reg8_2: pin names not known; wires that end beside it: 1'b0, 1'b0, 1'b0, 1'b0, 1'b0, CLK, 1'b1, mp2_8b_2_p3, DW[7:0], CREGBUS[4], 1'b0, 1'b0, CREGBUS[8], CREGBUS[9]
  // MP8_8b mp8_8b_1: pin names not known; wires that end beside it: CMEMBUS[10], CMEMBUS[9], CMEMBUS[8], DIN, A[15:8], A[7:0], PC[15:8], mp8_8b_1_p8, PC[7:0], {PSW[15], {7{1'b0}}}, {3'b000, PSW[4:0]}, 1'b1
  // REG8_LD reg8_ld_3: pin names not known; wires that end beside it: CLK, mp8_8b_1_p8, MDR, CMEMBUS[2]
  // REG8_LD reg8_ld_4: pin names not known; wires that end beside it: CLK, MDR, IR[15:8], CREGBUS[1]
  // REG8_LD reg8_ld_5: pin names not known; wires that end beside it: CLK, MDR, IR[7:0], CREGBUS[0]
  and and_6 (and_6_out, ~IR[23], adrinst_t);  // AND_Gate
  // DC3_8 dc3_8_4: pin names not known; wires that end beside it: IR[22:20], and_6_out, dc3_8_4_p3, dc3_8_4_p4, dc3_8_4_p5, ADDRBUS[3], ADDRBUS[4], ADDRBUS[5], ADDRBUS[6]
  // MP2_1b mp2_1b_1: pin names not known; wires that end beside it: INSTRUCBUS[4], A[0], mp2_1b_1_p3, PSW[4], 1'b1
  and and_7 (and_7_out, ~IR[19], ~IR[18], ~IR[17], ~IR[16]);  // AND_Gate
  // MP4_16b mp4_16b_1: pin names not known; wires that end beside it: CREGBUS[12], CREGBUS[11], DW, IR[15:0], mp4_16b_1_p5, {GPR15__0, GPR7__0}, 1'b1
  // REG16_LD reg16_ld_1: pin names not known; wires that end beside it: CLK, 1'b1, mp4_16b_1_p5, B, CREGBUS[10]
  and and_8 (ADDRBUS[0], and_7_out, dc3_8_4_p3);
  and and_9 (ADDRBUS[1], and_7_out, dc3_8_4_p4);
  and and_10 (ADDRBUS[2], and_7_out, dc3_8_4_p5);
  not not_1 (not_1_out, RST);
  // RSFF rsff_1: pin names not known; wires that end beside it: CFFBUS[1], CLK, CFFBUS[0], not_1_out, PHASEFFBUS[0]
  // MP8_16b mp8_16b_2: pin names not known; wires that end beside it: RST, CMEMBUS[12], CMEMBUS[11], MAR, DW, ALU, IR[23:8], mp8_16b_2_p8, 16'h1000, 1'b1
  // REG16_INC_LD reg16_inc_ld_2: pin names not known; wires that end beside it: CLK, mp8_16b_2_p8, PC, reg16_inc_ld_2_p4, CMEMBUS[4]
  // MP4_16b mp4_16b_2: pin names not known; wires that end beside it: CREGBUS[19], CREGBUS[18], DW, 1'b1, B, mp4_16b_2_p6, mp4_16b_2_p6, ALU, CNT, 1'b1
  // REG16 reg16_2: pin names not known; wires that end beside it: RST, CREGBUS[17], mp2_1b_1_p3, CLK, A, CREGBUS[16]
  or or_1 (reg16_inc_ld_2_p4, CMEMBUS[3], RST);
  Pull_Resistor pull_resistor_1 (.node(A));
  // RSFF rsff_2: pin names not known; wires that end beside it: CFFBUS[3], CLK, CFFBUS[2], rsff_2_p4, PHASEFFBUS[1]
  not not_2 (rsff_2_p4, RST);
  and and_11 (and_11_out, DW[2], INSTRUCBUS[2]);
  and and_12 (and_12_out, ADRINST, A[15]);
  and and_13 (and_13_out, ~A[15], ~B[15], ALU[15]);  // AND_Gate
  or or_2 (or_2_out, and_13_out, and_14_out);
  and and_14 (and_14_out, A[15], B[15], ~ALU[15]);  // AND_Gate
  or or_3 (or_3_out, INSTRUCBUS[3], INSTRUCBUS[4]);
  or or_4 (or_4_out, INSTRUCBUS[16], INSTRUCBUS[17]);
  // RSFF rsff_3: pin names not known; wires that end beside it: CFFBUS[5], CLK, CFFBUS[4], rsff_3_p4, PHASEFFBUS[2]
  not not_3 (rsff_3_p4, RST);
  nor nor_2 (nor_2_out, A[0], A[1], A[2], A[3], A[4], A[5], A[6], A[7], A[8], A[9], A[10], A[11], A[12], A[13], A[14], A[15]);
  or or_5 (or_5_out, and_11_out, and_12_out);
  and and_15 (and_15_out, INSTRUCBUS[16], or_2_out);
  and and_16 (and_16_out, INSTRUCBUS[17], ~B[15], ALU[15]);  // AND_Gate
  and and_17 (and_17_out, DW[4], INSTRUCBUS[2]);
  and and_18 (and_18_out, or_3_out, A[0]);
  and and_19 (and_19_out, or_4_out, C16);
  and and_20 (and_20_out, DW[15], INSTRUCBUS[2]);
  and and_21 (and_21_out, ~DW[0], INSTRUCBUS[2], CPSW[1]);  // AND_Gate
  or or_6 (or_6_out, and_21_out, CPSW[0]);
  and and_22 (and_22_out, DW[0], INSTRUCBUS[2], CPSW[1]);
  and and_23 (and_23_out, DW[1], INSTRUCBUS[2]);
  and and_24 (and_24_out, ADRINST, nor_2_out);
  and and_25 (and_25_out, ~or_5_out, CPSW[3]);  // AND_Gate
  and and_26 (and_26_out, or_5_out, CPSW[3]);
  and and_27 (and_27_out, DW[3], INSTRUCBUS[2]);
  or or_7 (or_7_out, and_17_out, and_18_out, and_19_out);
  and and_28 (and_28_out, ~and_20_out, CPSW[6]);  // AND_Gate
  and and_29 (and_29_out, and_20_out, CPSW[6]);
  // MP2_16b mp2_16b_1: pin names not known; wires that end beside it: CREGBUS[20], DW, mp2_16b_1_p3, A, 1'b1
  GPR16x16 gpr16x16_1 (
    .DI15__0(mp2_16b_1_p3), .A3__0(IR[19:16]), .WR(CREGBUS[13]), .CLK(CLK), .DO15__0({GPR15__0, GPR7__0}));
  not not_4 (not_4_out, RST);
  // RSFF rsff_4: pin names not known; wires that end beside it: or_6_out, CLK, and_22_out, not_4_out, PSW[0]
  or or_8 (or_8_out, and_23_out, and_24_out);
  or or_9 (or_9_out, and_27_out, and_15_out, and_16_out);
  and and_30 (and_30_out, ~or_7_out, CPSW[5]);  // AND_Gate
  and and_31 (and_31_out, or_7_out, CPSW[5]);
  not not_5 (not_5_out, RST);
  // RSFF rsff_5: pin names not known; wires that end beside it: and_28_out, CLK, and_29_out, not_5_out, PSW[15]
  // RSFF rsff_6: pin names not known; wires that end beside it: CFFBUS[7], CLK, CFFBUS[6], rsff_6_p4, PHASEFFBUS[3]
  not not_6 (rsff_6_p4, RST);
  or or_10 (ADRINST, INSTRUCBUS[6], INSTRUCBUS[3], INSTRUCBUS[4], INSTRUCBUS[14], INSTRUCBUS[16], INSTRUCBUS[17], INSTRUCBUS[18], INSTRUCBUS[19]);
  and and_32 (and_32_out, ~or_8_out, CPSW[2]);  // AND_Gate
  and and_33 (and_33_out, or_8_out, CPSW[2]);
  // RSFF rsff_7: pin names not known; wires that end beside it: and_25_out, CLK, and_26_out, rsff_7_p4, PSW[2]
  not not_7 (rsff_7_p4, RST);
  and and_34 (and_34_out, ~or_9_out, CPSW[4]);  // AND_Gate
  // RSFF rsff_8: pin names not known; wires that end beside it: and_34_out, CLK, rsff_8_p3, rsff_8_p4, PSW[3]
  and and_35 (rsff_8_p3, CPSW[4], or_9_out);
  not not_8 (rsff_8_p4, RST);
  // RSFF rsff_9: pin names not known; wires that end beside it: and_30_out, CLK, and_31_out, rsff_9_p4, PSW[4]
  not not_9 (rsff_9_p4, RST);
  // RSFF rsff_10: pin names not known; wires that end beside it: and_32_out, CLK, and_33_out, rsff_10_p4, PSW[1]
  not not_10 (rsff_10_p4, RST);

  assign PSW[14:5] = {10{1'b0}};

  // Other names for the same wires on the sheet: A7__0[7:0] = A[7:0]; A15__0[15:0] = A; A15__8[7:0] = A[15:8];
  //   immed = ADDRBUS[0]; memdir = ADDRBUS[1]; memind = ADDRBUS[2]; regind = ADDRBUS[3]; postincr = ADDRBUS[4];
  //   postdec = ADDRBUS[5]; regdir = ADDRBUS[6]; ALU15__0[15:0] = ALU; B15__0[15:0] = B; stFETCH = CFFBUS[0];
  //   clFETCH = CFFBUS[1]; stADDR = CFFBUS[2]; clADDR = CFFBUS[3]; stEXEC = CFFBUS[4]; clEXEC = CFFBUS[5];
  //   stINTR = CFFBUS[6]; clINTR = CFFBUS[7]; ldMAR = CMEMBUS[0]; incMAR = CMEMBUS[1]; ldMDR = CMEMBUS[2];
  //   ldPC = CMEMBUS[3]; incPC = CMEMBUS[4]; mxMAR0 = CMEMBUS[5]; mxMAR1 = CMEMBUS[6]; mxMAR2 = CMEMBUS[7];
  //   mxMDR0 = CMEMBUS[8]; mxMDR1 = CMEMBUS[9]; mxMDR2 = CMEMBUS[10]; mxPC0 = CMEMBUS[11]; mxPC1 = CMEMBUS[12];
  //   CNT15__0[15:0] = CNT; clPSWSTART = CPSW[0]; ldPSWSTART = CPSW[1]; ldZ = CPSW[2]; ldN = CPSW[3]; ldV = CPSW[4];
  //   ldC = CPSW[5]; ldI = CPSW[6]; ldIR7__0 = CREGBUS[0]; ldIR15__8 = CREGBUS[1]; ldIR23__16 = CREGBUS[2];
  //   ldIR31__24 = CREGBUS[3]; ldDWL = CREGBUS[4]; mxDWL0 = CREGBUS[5]; ldDWH = CREGBUS[6]; mxDWH0 = CREGBUS[7];
  //   incDW = CREGBUS[8]; decDW = CREGBUS[9]; ldB = CREGBUS[10]; mxB0 = CREGBUS[11]; mxB1 = CREGBUS[12];
  //   wrGPR = CREGBUS[13]; incSP = CREGBUS[14]; decSP = CREGBUS[15]; ldA = CREGBUS[16]; srA = CREGBUS[17];
  //   mxA0 = CREGBUS[18]; mxA1 = CREGBUS[19]; mxGPR0 = CREGBUS[20]; Din7__0[7:0] = DIN; DWL[7:0] = DW[7:0];
  //   DWL0 = DW[0]; DWL1 = DW[1]; DWL2 = DW[2]; DWL3 = DW[3]; DWL4 = DW[4]; DWL5 = DW[5]; DWL6 = DW[6]; DWL7 = DW[7];
  //   DWH[7:0] = DW[15:8]; ENTRADDR15__0[15:0] = IVTPPDSP; GPR15__0[7:0] = GPR7__0; GPR15__8[7:0] = GPR15__0;
  //   HALT = INSTRUCBUS[0]; RTS = INSTRUCBUS[1]; RTI = INSTRUCBUS[2]; ROR = INSTRUCBUS[3]; RORC = INSTRUCBUS[4];
  //   PUSH = INSTRUCBUS[5]; POP = INSTRUCBUS[6]; BLEQ = INSTRUCBUS[7]; BGREU = INSTRUCBUS[8]; BNNG = INSTRUCBUS[9];
  //   BGRT = INSTRUCBUS[10]; JLEQ = INSTRUCBUS[11]; JMP = INSTRUCBUS[12]; JSR = INSTRUCBUS[13]; LD = INSTRUCBUS[14];
  //   ST = INSTRUCBUS[15]; ADD = INSTRUCBUS[16]; INC = INSTRUCBUS[17]; OR = INSTRUCBUS[18]; STRFIND = INSTRUCBUS[19];
  //   IR7__0[7:0] = IR[7:0]; IR15__0[15:0] = IR[15:0]; IR15__8[7:0] = IR[15:8]; IR23__8[15:0] = IR[23:8];
  //   IR19__16[3:0] = IR[19:16]; IR23__16[7:0] = IR[23:16]; IR22__20[2:0] = IR[22:20]; IR26__24[2:0] = IR[26:24];
  //   IR31__24[7:0] = IR[31:24]; MAR15__0[15:0] = MAR; MDR7__0[7:0] = MDR; PC7__0[7:0] = PC[7:0]; PC15__0[15:0] = PC;
  //   PC15__8[7:0] = PC[15:8]; FETCH = PHASEFFBUS[0]; ADDR = PHASEFFBUS[1]; EXEC = PHASEFFBUS[2];
  //   INTR = PHASEFFBUS[3]; PSW7__0[4:0] = PSW[4:0]; PSW15__0 (some bits) = {PSW[15], PSW[4:0]}; PSWSTART = PSW[0];
  //   PSWZ = PSW[1]; PSWN = PSW[2]; PSWV = PSW[3]; PSWC = PSW[4]; PSW15__8[7] = PSW[15]; PSWI = PSW[15]

  // Notes on the sheet:
  //   Stek
  //   Instrukcijski registar
  //   Pomocni registri
  //   MAR
  //   Dekoderi za prepoznavanje instrukcije na osnovu sadrzaja registra IR23..16
  //   MDR
  //   Akumulator
  //   PC
  //   FF za pokretanje FETCH, ADDR, EXEC i INTR faze izvršavanja instrukcije
  //   Registri opste namene
  //   Programska statusna reč (PSW)
endmodule

module FETCH (
  input  in_1,
  input  in_2,
  input  in_3,
  input  [3:0] PHASEFFBUS,
  input  [19:0] INSTRUCBUS,
  input  [6:0] ADDRBUS,
  input  [15:0] PSW,
  output [23:0] CMEMBUS,
  output [23:0] CFFBUS,
  output [23:0] CREGBUS,
  output rdMEM
);

  wire adr2, and_2_out, and_4_out, and_5_out, and_6_out, and_7_out, and_8_out, and_9_out, and_10_out,
       and_11_out, bezadr1, bradr2, brbezadr1, brcnd, brgradr, brgropr, brjmp2, brjmp3, brnotfcbus, bruncnd,
       clFETCH, gradr, grinst, gropr, incPC, jmp2, jmp3, ldIR7__0, ldIR15__8, ldIR23__16, ldIR31__24, ldMAR,
       ldMDR, nand_1_out, nor_1_out, not_1_out, not_2_out, notPSWSTandFETCH, or_4_out, or_5_out, or_6_out,
       or_7_out, or_8_out, rdMEM_t, stADDR, stEXEC;
  wire [4:0] reg5_inc_ld_1_a4__0;
  wire [19:11] dc4_16_1_p1;

  or or_1 (bezadr1, INSTRUCBUS[0], INSTRUCBUS[1], INSTRUCBUS[2], INSTRUCBUS[3], INSTRUCBUS[4], INSTRUCBUS[5], INSTRUCBUS[6]);
  or or_2 (jmp2, INSTRUCBUS[7], INSTRUCBUS[8], INSTRUCBUS[9], INSTRUCBUS[10]);
  not not_1 (not_1_out, in_1);
  REG5_INC_LD reg5_inc_ld_1 (
    .I4__0(dc4_16_1_p1[19:15]), .LD(or_4_out), .INC(not_2_out), .mr(not_1_out), .CLK(in_2),
    .A4__0(reg5_inc_ld_1_a4__0));
  // DC4_16 dc4_16_1: pin names not known; wires that end beside it: dc4_16_1_p1[14:11], 1'b1, bruncnd, notPSWSTandFETCH, brbezadr1, brjmp2, bradr2, brjmp3, brnotfcbus, brgropr, brgradr
  or or_3 (jmp3, INSTRUCBUS[11], INSTRUCBUS[12], INSTRUCBUS[13]);
  not not_2 (not_2_out, or_4_out);
  ROM32x20 rom32x20_1 (
    .A4__0(reg5_inc_ld_1_a4__0), .CS(1'b1),
    .DOUT19__0({dc4_16_1_p1, stEXEC, stADDR, clFETCH, ldIR7__0, ldIR15__8, ldIR23__16, ldIR31__24, rdMEM_t, ldMDR, incPC, ldMAR}));
  or or_4 (or_4_out, brcnd, bruncnd);
  or or_5 (or_5_out, INSTRUCBUS[14], INSTRUCBUS[15], INSTRUCBUS[16], INSTRUCBUS[17], INSTRUCBUS[18], INSTRUCBUS[19]);
  or or_6 (or_6_out, ADDRBUS[3], ADDRBUS[4], ADDRBUS[5], ADDRBUS[6]);
  and and_1 (adr2, or_6_out, or_5_out);
  nor nor_1 (nor_1_out, ADDRBUS[0], ADDRBUS[1], ADDRBUS[2], ADDRBUS[3], ADDRBUS[4], ADDRBUS[5], ADDRBUS[6]);
  and and_2 (and_2_out, INSTRUCBUS[15], ADDRBUS[0]);
  or or_7 (or_7_out, INSTRUCBUS[14], INSTRUCBUS[15], INSTRUCBUS[16], INSTRUCBUS[17], INSTRUCBUS[18], INSTRUCBUS[19]);
  or or_8 (or_8_out, nor_1_out, and_2_out);
  and and_3 (gradr, or_7_out, or_8_out);
  nand nand_1 (nand_1_out, PSW[0], PHASEFFBUS[0]);
  and and_4 (and_4_out, nand_1_out, notPSWSTandFETCH);
  and and_5 (and_5_out, brbezadr1, bezadr1);
  and and_6 (and_6_out, brjmp2, jmp2);
  and and_7 (and_7_out, bradr2, adr2);
  and and_8 (and_8_out, brjmp3, jmp3);
  and and_9 (and_9_out, brnotfcbus, ~in_3);  // AND_Gate
  and and_10 (and_10_out, brgropr, gropr);
  and and_11 (and_11_out, brgradr, gradr);
  nor nor_2 (gropr, INSTRUCBUS[0], INSTRUCBUS[1], INSTRUCBUS[2], INSTRUCBUS[3], INSTRUCBUS[4], INSTRUCBUS[5], INSTRUCBUS[6], INSTRUCBUS[7], INSTRUCBUS[8], INSTRUCBUS[9], INSTRUCBUS[10], INSTRUCBUS[11], INSTRUCBUS[12], INSTRUCBUS[13], INSTRUCBUS[14], INSTRUCBUS[15], INSTRUCBUS[16], INSTRUCBUS[17], INSTRUCBUS[18], INSTRUCBUS[19]);
  or or_9 (brcnd, and_4_out, and_5_out, and_6_out, and_7_out, and_8_out, and_9_out, and_10_out, and_11_out);
  or or_10 (grinst, gropr, gradr);
  assign CFFBUS[4] = stEXEC ? 1'b1 : 1'bz;  // Controlled_Buffer controlled_buffer_1
  assign CREGBUS[2] = ldIR23__16 ? 1'b1 : 1'bz;  // Controlled_Buffer controlled_buffer_2
  assign CREGBUS[3] = ldIR31__24 ? 1'b1 : 1'bz;  // Controlled_Buffer controlled_buffer_3
  assign CMEMBUS[2] = ldMDR ? 1'b1 : 1'bz;  // Controlled_Buffer controlled_buffer_4
  assign CMEMBUS[4] = incPC ? 1'b1 : 1'bz;  // Controlled_Buffer controlled_buffer_5
  assign CFFBUS[2] = stADDR ? 1'b1 : 1'bz;  // Controlled_Buffer controlled_buffer_6
  assign CREGBUS[1] = ldIR15__8 ? 1'b1 : 1'bz;  // Controlled_Buffer controlled_buffer_7
  assign CMEMBUS[0] = ldMAR ? 1'b1 : 1'bz;  // Controlled_Buffer controlled_buffer_8
  assign CFFBUS[1] = clFETCH ? 1'b1 : 1'bz;  // Controlled_Buffer controlled_buffer_9
  assign CREGBUS[0] = ldIR7__0 ? 1'b1 : 1'bz;  // Controlled_Buffer controlled_buffer_10
  assign rdMEM = rdMEM_t ? 1'b1 : 1'bz;  // Controlled_Buffer controlled_buffer_11

  // Other names for the same wires on the sheet: immed = ADDRBUS[0]; memdir = ADDRBUS[1]; memind = ADDRBUS[2];
  //   regind = ADDRBUS[3]; postincr = ADDRBUS[4]; postdec = ADDRBUS[5]; regdir = ADDRBUS[6]; CLK = in_2; FCBUS = in_3;
  //   HALT = INSTRUCBUS[0]; RTS = INSTRUCBUS[1]; RTI = INSTRUCBUS[2]; ROR = INSTRUCBUS[3]; RORC = INSTRUCBUS[4];
  //   PUSH = INSTRUCBUS[5]; POP = INSTRUCBUS[6]; BLEQ = INSTRUCBUS[7]; BGREU = INSTRUCBUS[8]; BNNG = INSTRUCBUS[9];
  //   BGRT = INSTRUCBUS[10]; JLEQ = INSTRUCBUS[11]; JMP = INSTRUCBUS[12]; JSR = INSTRUCBUS[13]; LD = INSTRUCBUS[14];
  //   ST = INSTRUCBUS[15]; ADD = INSTRUCBUS[16]; INC = INSTRUCBUS[17]; OR = INSTRUCBUS[18]; STRFIND = INSTRUCBUS[19];
  //   FETCH = PHASEFFBUS[0]; ADDR = PHASEFFBUS[1]; EXEC = PHASEFFBUS[2]; INTR = PHASEFFBUS[3]; PSWSTART = PSW[0];
  //   rst = in_1

  // Notes on the sheet:
  //   Operaciona jedinica
  //   Kontrolna jedinica
endmodule

module ADDR (
  input  in_1,
  input  in_2,
  input  in_3,
  input  [3:0] PHASEFFBUS,
  input  [19:0] INSTRUCBUS,
  input  [6:0] ADDRBUS,
  output [23:0] CMEMBUS,
  output [23:0] CFFBUS,
  output [23:0] CREGBUS,
  output rdMEM
);

  wire and_1_out, and_2_out, and_3_out, bradr, brcnd, brnotaddr, brnotfcbus, brst, bruncnd, clADDR, decDW,
       incDW, incMAR, ldB, ldDWH, ldDWL, ldMAR, ldMDR, mxB0, mxB1, mxDWH0, mxDWL0, mxMAR0, mxMAR1, not_1_out,
       not_2_out, or_1_out, rdMEM_t, stEXEC, wrGRP;
  wire [2:0] dc3_8_1_p1;
  wire [4:0] kmadr7_1_adr4__0, mp2_5b_1_y, reg5_inc_ld_1_a4__0, rom32x26_1_dout23__0;

  // DC3_8 dc3_8_1: pin names not known; wires that end beside it: dc3_8_1_p1, 1'b1, bruncnd, brnotaddr, brnotfcbus, brst, bradr
  not not_1 (not_1_out, in_1);
  KMADR7 kmadr7_1 (
    .immed(ADDRBUS[0]), .memdir(ADDRBUS[1]), .memind(ADDRBUS[2]), .regind(ADDRBUS[3]), .postincr(ADDRBUS[4]),
    .postdec(ADDRBUS[5]), .regdir(ADDRBUS[6]), .Adr4__0(kmadr7_1_adr4__0));
  MP2_5b mp2_5b_1 (.En(1'b1), .in_2(rom32x26_1_dout23__0), .in_3(kmadr7_1_adr4__0), .S0(bradr), .Y(mp2_5b_1_y));
  REG5_INC_LD reg5_inc_ld_1 (
    .I4__0(mp2_5b_1_y), .LD(or_1_out), .INC(not_2_out), .mr(not_1_out), .CLK(in_2),
    .A4__0(reg5_inc_ld_1_a4__0));
  or or_1 (or_1_out, bruncnd, brcnd, bradr);
  not not_2 (not_2_out, or_1_out);
  ROM32x26 rom32x26_1 (
    .A4__0(reg5_inc_ld_1_a4__0), .CS(1'b1),
    .DOUT23__0({rom32x26_1_dout23__0, dc3_8_1_p1, stEXEC, clADDR, wrGRP, mxB1, mxB0, ldB, decDW, incDW, mxDWH0, mxDWL0, ldDWH, ldDWL, mxMAR1, mxMAR0, rdMEM_t, ldMDR, incMAR, ldMAR}));
  and and_1 (and_1_out, brnotaddr, ~PHASEFFBUS[1]);  // AND_Gate
  and and_2 (and_2_out, brst, INSTRUCBUS[15]);
  and and_3 (and_3_out, brnotfcbus, ~in_3);  // AND_Gate
  or or_2 (brcnd, and_1_out, and_2_out, and_3_out);
  assign CMEMBUS[6] = mxMAR1 ? 1'b1 : 1'bz;  // Controlled_Buffer controlled_buffer_1
  assign CMEMBUS[5] = mxMAR0 ? 1'b1 : 1'bz;  // Controlled_Buffer controlled_buffer_2
  assign CREGBUS[11] = mxB0 ? 1'b1 : 1'bz;  // Controlled_Buffer controlled_buffer_3
  assign CREGBUS[13] = wrGRP ? 1'b1 : 1'bz;  // Controlled_Buffer controlled_buffer_4
  assign CMEMBUS[1] = incMAR ? 1'b1 : 1'bz;  // Controlled_Buffer controlled_buffer_5
  assign CMEMBUS[2] = ldMDR ? 1'b1 : 1'bz;  // Controlled_Buffer controlled_buffer_6
  assign CFFBUS[4] = stEXEC ? 1'b1 : 1'bz;  // Controlled_Buffer controlled_buffer_7
  assign CREGBUS[9] = decDW ? 1'b1 : 1'bz;  // Controlled_Buffer controlled_buffer_8
  assign CREGBUS[10] = ldB ? 1'b1 : 1'bz;  // Controlled_Buffer controlled_buffer_9
  assign CREGBUS[12] = mxB1 ? 1'b1 : 1'bz;  // Controlled_Buffer controlled_buffer_10
  assign CMEMBUS[0] = ldMAR ? 1'b1 : 1'bz;  // Controlled_Buffer controlled_buffer_11
  assign CFFBUS[3] = clADDR ? 1'b1 : 1'bz;  // Controlled_Buffer controlled_buffer_12
  assign CREGBUS[6] = ldDWH ? 1'b1 : 1'bz;  // Controlled_Buffer controlled_buffer_13
  assign CREGBUS[7] = mxDWH0 ? 1'b1 : 1'bz;  // Controlled_Buffer controlled_buffer_14
  assign CREGBUS[8] = incDW ? 1'b1 : 1'bz;  // Controlled_Buffer controlled_buffer_15
  assign CREGBUS[5] = mxDWL0 ? 1'b1 : 1'bz;  // Controlled_Buffer controlled_buffer_16
  assign rdMEM = rdMEM_t ? 1'b1 : 1'bz;  // Controlled_Buffer controlled_buffer_17
  assign CREGBUS[4] = ldDWL ? 1'b1 : 1'bz;  // Controlled_Buffer controlled_buffer_18

  // Other names for the same wires on the sheet: immed = ADDRBUS[0]; memdir = ADDRBUS[1]; memind = ADDRBUS[2];
  //   regind = ADDRBUS[3]; postincr = ADDRBUS[4]; postdec = ADDRBUS[5]; regdir = ADDRBUS[6]; CLK = in_2; FCBUS = in_3;
  //   HALT = INSTRUCBUS[0]; RTS = INSTRUCBUS[1]; RTI = INSTRUCBUS[2]; ROR = INSTRUCBUS[3]; RORC = INSTRUCBUS[4];
  //   PUSH = INSTRUCBUS[5]; POP = INSTRUCBUS[6]; BLEQ = INSTRUCBUS[7]; BGREU = INSTRUCBUS[8]; BNNG = INSTRUCBUS[9];
  //   BGRT = INSTRUCBUS[10]; JLEQ = INSTRUCBUS[11]; JMP = INSTRUCBUS[12]; JSR = INSTRUCBUS[13]; LD = INSTRUCBUS[14];
  //   ST = INSTRUCBUS[15]; ADD = INSTRUCBUS[16]; INC = INSTRUCBUS[17]; OR = INSTRUCBUS[18]; STRFIND = INSTRUCBUS[19];
  //   FETCH = PHASEFFBUS[0]; ADDR = PHASEFFBUS[1]; EXEC = PHASEFFBUS[2]; INTR = PHASEFFBUS[3]; rst = in_1

  // Notes on the sheet:
  //   Operaciona jedinica
  //   Upravljacka jedinica
endmodule

module EXEC (
  input  in_1,
  input  in_2,
  input  in_3,
  input  [7:0] MDR,
  input  [15:0] A,
  input  [15:0] B,
  input  [15:0] PC,
  input  [31:0] IR,
  input  [3:0] PHASEFFBUS,
  input  [19:0] INSTRUCBUS,
  input  [6:0] ADDRBUS,
  input  [15:0] PSW,
  output [15:0] ALU,
  output [15:0] CNT,
  output C16,
  output [23:0] CMEMBUS,
  output [23:0] CFFBUS,
  output [23:0] CREGBUS,
  output [6:0] CPSW,
  output rdMEM,
  output wrMEM
);

  wire add_t, and_1_out, and_2_out, and_3_out, and_4_out, and_5_out, and_6_out, and_7_out, and_8_out,
       and_9_out, and_10_out, and_11_out, brcnd, brequal, brnotbrorjmp, brnotend, brnotexec, brnotfcbus,
       brnotregdir, bropr, brorjmp, bruncnd, clCNT, clEXEC, clPSWSTART, dc4_16_1_p3, decSP, END, EQUAL,
       inc_t, incCNT, incMAR, incSP, ldA, ldC, ldCNT, ldDWH, ldDWL, ldI, ldMAR, ldMDR, ldN, ldPC, ldPSWSTART,
       ldV, ldZ, mxA0, mxA1, mxALU0, mxALU1, mxALU2, mxGPR0, mxMAR0, mxMAR2, mxMDR0, mxMDR1, mxMDR2, mxPC0,
       mxPC1, not_1_out, not_2_out, not_3_out, or_1_out, or_2_out, or_t, rdMEM_t, srA, stINTR, wrGPR,
       wrMEM_t, xor_1_out;
  wire [3:0] dc4_16_1_p1;
  wire [6:0] kmopr20_1_adr6__0, mp2_7b_1_out_5, reg7_inc_ld_1_a6__0;
  wire [15:0] mp2_16b_1_p3, mp4_16b_1_p5;
  wire [19:13] rom128x52_1_dout51__32;

  xor xor_1 (xor_1_out, PSW[2], PSW[3]);
  or or_1 (or_1_out, xor_1_out, PSW[1]);
  MP2_7b mp2_7b_1 (
    .En(1'b1), .in_2(rom128x52_1_dout51__32), .in_3(kmopr20_1_adr6__0), .S0(bropr), .out_5(mp2_7b_1_out_5));
  not not_1 (not_1_out, in_1);
  REG7_INC_LD reg7_inc_ld_1 (
    .I6__0(mp2_7b_1_out_5), .LD(or_2_out), .INC(not_2_out), .mr(not_1_out), .CLK(in_2),
    .A6__0(reg7_inc_ld_1_a6__0));
  // DC4_16 dc4_16_1: pin names not known; wires that end beside it: dc4_16_1_p1, 1'b1, dc4_16_1_p3, bruncnd, brnotexec, brnotfcbus, brnotbrorjmp, brnotregdir, brequal, brnotend, bropr, dc4_16_1_p3
  KMOPR20 kmopr20_1 (.inst19__0(INSTRUCBUS), .Adr6__0(kmopr20_1_adr6__0));
  not not_2 (not_2_out, or_2_out);
  ROM128x52 rom128x52_1 (
    .A6__0(reg7_inc_ld_1_a6__0), .CS(1'b1),
    .DOUT51__32({rom128x52_1_dout51__32, dc4_16_1_p1, stINTR, clEXEC, ldI, ldC, ldV, ldN, ldZ, ldPSWSTART, clPSWSTART}),
    .DOUT31__0({mxALU2, mxALU1, mxALU0, or_t, inc_t, add_t, clCNT, incCNT, ldCNT, mxGPR0, wrGPR, ldDWH, ldDWL, mxA1, mxA0, srA, ldA, decSP, incSP, mxPC1, mxPC0, ldPC, mxMAR2, mxMAR0, mxMDR2, mxMDR1, mxMDR0, wrMEM_t, rdMEM_t, ldMDR, incMAR, ldMAR}));
  and and_1 (and_1_out, INSTRUCBUS[7], or_1_out);
  and and_2 (and_2_out, INSTRUCBUS[10], ~or_1_out);  // AND_Gate
  and and_3 (and_3_out, INSTRUCBUS[11], or_1_out);
  and and_4 (and_4_out, INSTRUCBUS[8], ~PSW[4]);  // AND_Gate
  and and_5 (and_5_out, INSTRUCBUS[9], ~PSW[2]);  // AND_Gate
  or or_2 (or_2_out, bruncnd, brcnd, bropr);
  or or_3 (brorjmp, and_1_out, and_2_out, and_3_out, and_4_out, and_5_out);
  not not_3 (not_3_out, in_1);
  REG16_CL_INC_LD reg16_cl_inc_ld_1 (
    .I15__0({16{1'b1}}), .LD(ldCNT), .CL(clCNT), .INC(incCNT), .mr(not_3_out), .CLK(in_2), .out_7(CNT));
  Comparator #(.mode("unsigned")) comparator_1 (.a(MDR), .b(A[7:0]), .eq(EQUAL));  // open: gt, lt
  Comparator #(.mode("unsigned")) comparator_2 (.a(MDR), .b({8{1'b0}}), .eq(END));  // open: gt, lt
  // MP2_16b mp2_16b_1: pin names not known; wires that end beside it: mxALU2, A, mp2_16b_1_p3, PC, 1'b1
  Pull_Resistor pull_resistor_1 (.node(ALU));
  ALU16_ADD_INC_OR alu16_add_inc_or_1 (
    .add(add_t), .inc(inc_t), .\or (or_t), .DOUT15__0(ALU), .Cout(C16), .A15__0(mp2_16b_1_p3),
    .B15__0(mp4_16b_1_p5));
  // MP4_16b mp4_16b_1: pin names not known; wires that end beside it: mxALU1, mxALU0, B, {{8{1'b0}}, IR[23:16]}, mp4_16b_1_p5, {{9{IR[23]}}, IR[22:16]}, 1'b1
  Pull_Resistor pull_resistor_2 (.node(C16));
  and and_6 (and_6_out, brnotexec, ~PHASEFFBUS[2]);  // AND_Gate
  and and_7 (and_7_out, brnotfcbus, ~in_3);  // AND_Gate
  and and_8 (and_8_out, brnotbrorjmp, ~brorjmp);  // AND_Gate
  and and_9 (and_9_out, brnotregdir, ~ADDRBUS[6]);  // AND_Gate
  and and_10 (and_10_out, brequal, EQUAL);
  and and_11 (and_11_out, brnotend, ~END);  // AND_Gate
  or or_4 (brcnd, and_6_out, and_7_out, and_8_out, and_9_out, and_10_out, and_11_out);
  assign CPSW[5] = ldC ? 1'b1 : 1'bz;  // Controlled_Buffer controlled_buffer_1
  assign CPSW[6] = ldI ? 1'b1 : 1'bz;  // Controlled_Buffer controlled_buffer_2
  assign CMEMBUS[5] = mxMAR0 ? 1'b1 : 1'bz;  // Controlled_Buffer controlled_buffer_3
  assign CMEMBUS[7] = mxMAR2 ? 1'b1 : 1'bz;  // Controlled_Buffer controlled_buffer_4
  assign CMEMBUS[8] = mxMDR0 ? 1'b1 : 1'bz;  // Controlled_Buffer controlled_buffer_5
  assign CPSW[3] = ldN ? 1'b1 : 1'bz;  // Controlled_Buffer controlled_buffer_6
  assign CPSW[4] = ldV ? 1'b1 : 1'bz;  // Controlled_Buffer controlled_buffer_7
  assign CMEMBUS[3] = ldPC ? 1'b1 : 1'bz;  // Controlled_Buffer controlled_buffer_8
  assign CMEMBUS[9] = mxMDR1 ? 1'b1 : 1'bz;  // Controlled_Buffer controlled_buffer_9
  assign CREGBUS[16] = ldA ? 1'b1 : 1'bz;  // Controlled_Buffer controlled_buffer_10
  assign CREGBUS[17] = srA ? 1'b1 : 1'bz;  // Controlled_Buffer controlled_buffer_11
  assign CPSW[2] = ldZ ? 1'b1 : 1'bz;  // Controlled_Buffer controlled_buffer_12
  assign CMEMBUS[1] = incMAR ? 1'b1 : 1'bz;  // Controlled_Buffer controlled_buffer_13
  assign CMEMBUS[2] = ldMDR ? 1'b1 : 1'bz;  // Controlled_Buffer controlled_buffer_14
  assign CMEMBUS[10] = mxMDR2 ? 1'b1 : 1'bz;  // Controlled_Buffer controlled_buffer_15
  assign CMEMBUS[11] = mxPC0 ? 1'b1 : 1'bz;  // Controlled_Buffer controlled_buffer_16
  assign CFFBUS[6] = stINTR ? 1'b1 : 1'bz;  // Controlled_Buffer controlled_buffer_17
  assign CREGBUS[6] = ldDWH ? 1'b1 : 1'bz;  // Controlled_Buffer controlled_buffer_18
  assign CREGBUS[14] = incSP ? 1'b1 : 1'bz;  // Controlled_Buffer controlled_buffer_19
  assign CREGBUS[15] = decSP ? 1'b1 : 1'bz;  // Controlled_Buffer controlled_buffer_20
  assign CREGBUS[18] = mxA0 ? 1'b1 : 1'bz;  // Controlled_Buffer controlled_buffer_21
  assign CREGBUS[19] = mxA1 ? 1'b1 : 1'bz;  // Controlled_Buffer controlled_buffer_22
  assign CPSW[1] = ldPSWSTART ? 1'b1 : 1'bz;  // Controlled_Buffer controlled_buffer_23
  assign CMEMBUS[0] = ldMAR ? 1'b1 : 1'bz;  // Controlled_Buffer controlled_buffer_24
  assign CMEMBUS[12] = mxPC1 ? 1'b1 : 1'bz;  // Controlled_Buffer controlled_buffer_25
  assign CFFBUS[5] = clEXEC ? 1'b1 : 1'bz;  // Controlled_Buffer controlled_buffer_26
  assign CREGBUS[4] = ldDWL ? 1'b1 : 1'bz;  // Controlled_Buffer controlled_buffer_27
  assign CREGBUS[13] = wrGPR ? 1'b1 : 1'bz;  // Controlled_Buffer controlled_buffer_28
  assign CREGBUS[20] = mxGPR0 ? 1'b1 : 1'bz;  // Controlled_Buffer controlled_buffer_29
  assign CPSW[0] = clPSWSTART ? 1'b1 : 1'bz;  // Controlled_Buffer controlled_buffer_30
  assign rdMEM = rdMEM_t ? 1'b1 : 1'bz;  // Controlled_Buffer controlled_buffer_31
  assign wrMEM = wrMEM_t ? 1'b1 : 1'bz;  // Controlled_Buffer controlled_buffer_32

  // Other names for the same wires on the sheet: IR23__16[7:0] = IR[23:16]; A7__0[7:0] = A[7:0]; A15__0[15:0] = A;
  //   immed = ADDRBUS[0]; memdir = ADDRBUS[1]; memind = ADDRBUS[2]; regind = ADDRBUS[3]; postincr = ADDRBUS[4];
  //   postdec = ADDRBUS[5]; regdir = ADDRBUS[6]; ALU15__0[15:0] = ALU; B15__0[15:0] = B; CLK = in_2;
  //   CNT15__0[15:0] = CNT; FCBUS = in_3; HALT = INSTRUCBUS[0]; Instr19__0[19:0] = INSTRUCBUS; RTS = INSTRUCBUS[1];
  //   RTI = INSTRUCBUS[2]; ROR = INSTRUCBUS[3]; RORC = INSTRUCBUS[4]; PUSH = INSTRUCBUS[5]; POP = INSTRUCBUS[6];
  //   BLEQ = INSTRUCBUS[7]; BGREU = INSTRUCBUS[8]; BNNG = INSTRUCBUS[9]; BGRT = INSTRUCBUS[10]; JLEQ = INSTRUCBUS[11];
  //   JMP = INSTRUCBUS[12]; JSR = INSTRUCBUS[13]; LD = INSTRUCBUS[14]; ST = INSTRUCBUS[15]; ADD = INSTRUCBUS[16];
  //   INC = INSTRUCBUS[17]; OR = INSTRUCBUS[18]; STRFIND = INSTRUCBUS[19]; IR7__0[7:0] = IR[7:0];
  //   IR15__8[7:0] = IR[15:8]; IR31__24[7:0] = IR[31:24]; MDR7__0[7:0] = MDR; PC15__0[15:0] = PC;
  //   FETCH = PHASEFFBUS[0]; ADDR = PHASEFFBUS[1]; EXEC = PHASEFFBUS[2]; INTR = PHASEFFBUS[3]; PSWSTART = PSW[0];
  //   PSWZ = PSW[1]; PSWN = PSW[2]; PSWV = PSW[3]; PSWC = PSW[4]; PSWI = PSW[15]; rst = in_1

  // Notes on the sheet:
  //   Uslov za skok
  //   Operaciona jedinica
  //   Upravljacka jedinica
  //   Brojac za indeks
  //   ALU
endmodule

module INTR (
  input  in_1,
  input  in_2,
  input  in_3,
  input  [3:0] PHASEFFBUS,
  input  [19:0] INSTRUCBUS,
  input  [15:0] PSW,
  input  [3:0] intr,
  output [15:0] ADDIVTP,
  output [1:0] UEXT1__0,
  output inta,
  output [23:0] CMEMBUS,
  output [23:0] CFFBUS,
  output [23:0] CREGBUS,
  output rdMEM,
  output wrMEM
);

  wire and_2_out, and_3_out, and_4_out, brcnd, brnotfcbus, brnotintr, brnotprekid, bruncnd, clINTR,
       dc3_8_1_p3, decSP, incMAR, ldDWH, ldDWL, ldMAR, ldMDR, ldPC, mxMAR1, mxMAR2, mxMDR0, mxMDR1, mxMDR2,
       mxPC0, not_1_out, not_2_out, not_3_out, or_1_out, pcd4_1_w, prekid, rdMEM_t, stFETCH, wrMEM_t;
  wire [2:0] dc3_8_1_p1;
  wire [2:1] IVTDSP15__0;
  wire [4:0] reg5_inc_ld_1_a4__0, rom32x26_2_1_dout23__0;
  wire [15:0] IVTP15__0;

  // DC3_8 dc3_8_1: pin names not known; wires that end beside it: dc3_8_1_p1, 1'b1, dc3_8_1_p3, bruncnd, brnotintr, brnotprekid, brnotfcbus, dc3_8_1_p3
  and and_1 (prekid, pcd4_1_w, PSW[15], PSW[0]);
  not not_1 (not_1_out, in_1);
  // REG16_LD reg16_ld_1: pin names not known; wires that end beside it: in_2, not_1_out, IVTP15__0
  not not_2 (not_2_out, in_1);
  REG5_INC_LD reg5_inc_ld_1 (
    .I4__0(rom32x26_2_1_dout23__0), .LD(or_1_out), .INC(not_3_out), .mr(not_2_out), .CLK(in_2),
    .A4__0(reg5_inc_ld_1_a4__0));
  not not_3 (not_3_out, or_1_out);
  ROM32x26_2 rom32x26_2_1 (
    .A4__0(reg5_inc_ld_1_a4__0), .CS(1'b1),
    .DOUT23__0({rom32x26_2_1_dout23__0, dc3_8_1_p1, stFETCH, clINTR, inta, decSP, ldDWH, ldDWL, mxPC0, ldPC, mxMAR2, mxMAR1, mxMDR2, mxMDR1, mxMDR0, wrMEM_t, rdMEM_t, ldMDR, incMAR, ldMAR}));
  or or_1 (or_1_out, bruncnd, brcnd);
  pCD4 pcd4_1 (
    .En(1'b1), .C3(intr[3]), .C2(intr[2]), .C1(intr[1]), .C0(intr[0]), .Z1(UEXT1__0[1]), .Z0(UEXT1__0[0]),
    .W(pcd4_1_w));
  // REG2_LD reg2_ld_1: pin names not known; wires that end beside it: in_2, UEXT1__0, IVTDSP15__0, inta
  and and_2 (and_2_out, brnotintr, ~PHASEFFBUS[3]);  // AND_Gate
  and and_3 (and_3_out, brnotprekid, ~prekid);  // AND_Gate
  and and_4 (and_4_out, brnotfcbus, ~in_3);  // AND_Gate
  or or_2 (brcnd, and_2_out, and_3_out, and_4_out);
  // ADD16 add16_1: pin names not known; wires that end beside it: IVTP15__0, ADDIVTP, {{13{1'b0}}, IVTDSP15__0, 1'b0}, 1'b0
  assign CMEMBUS[6] = mxMAR1 ? 1'b1 : 1'bz;  // Controlled_Buffer controlled_buffer_1
  assign CMEMBUS[3] = ldPC ? 1'b1 : 1'bz;  // Controlled_Buffer controlled_buffer_2
  assign CMEMBUS[7] = mxMAR2 ? 1'b1 : 1'bz;  // Controlled_Buffer controlled_buffer_3
  assign CMEMBUS[2] = ldMDR ? 1'b1 : 1'bz;  // Controlled_Buffer controlled_buffer_4
  assign CMEMBUS[8] = mxMDR0 ? 1'b1 : 1'bz;  // Controlled_Buffer controlled_buffer_5
  assign CMEMBUS[9] = mxMDR1 ? 1'b1 : 1'bz;  // Controlled_Buffer controlled_buffer_6
  assign CMEMBUS[1] = incMAR ? 1'b1 : 1'bz;  // Controlled_Buffer controlled_buffer_7
  assign CMEMBUS[10] = mxMDR2 ? 1'b1 : 1'bz;  // Controlled_Buffer controlled_buffer_8
  assign CREGBUS[6] = ldDWH ? 1'b1 : 1'bz;  // Controlled_Buffer controlled_buffer_9
  assign CMEMBUS[0] = ldMAR ? 1'b1 : 1'bz;  // Controlled_Buffer controlled_buffer_10
  assign CMEMBUS[11] = mxPC0 ? 1'b1 : 1'bz;  // Controlled_Buffer controlled_buffer_11
  assign CFFBUS[0] = stFETCH ? 1'b1 : 1'bz;  // Controlled_Buffer controlled_buffer_12
  assign CFFBUS[7] = clINTR ? 1'b1 : 1'bz;  // Controlled_Buffer controlled_buffer_13
  assign CREGBUS[4] = ldDWL ? 1'b1 : 1'bz;  // Controlled_Buffer controlled_buffer_14
  assign CREGBUS[15] = decSP ? 1'b1 : 1'bz;  // Controlled_Buffer controlled_buffer_15
  assign rdMEM = rdMEM_t ? 1'b1 : 1'bz;  // Controlled_Buffer controlled_buffer_16
  assign wrMEM = wrMEM_t ? 1'b1 : 1'bz;  // Controlled_Buffer controlled_buffer_17

  // Other names for the same wires on the sheet: ldBR = inta; ADDIVTP15__0[15:0] = ADDIVTP; CLK = in_2; FCBUS = in_3;
  //   HALT = INSTRUCBUS[0]; RTS = INSTRUCBUS[1]; RTI = INSTRUCBUS[2]; ROR = INSTRUCBUS[3]; RORC = INSTRUCBUS[4];
  //   PUSH = INSTRUCBUS[5]; POP = INSTRUCBUS[6]; BLEQ = INSTRUCBUS[7]; BGREU = INSTRUCBUS[8]; BNNG = INSTRUCBUS[9];
  //   BGRT = INSTRUCBUS[10]; JLEQ = INSTRUCBUS[11]; JMP = INSTRUCBUS[12]; JSR = INSTRUCBUS[13]; LD = INSTRUCBUS[14];
  //   ST = INSTRUCBUS[15]; ADD = INSTRUCBUS[16]; INC = INSTRUCBUS[17]; OR = INSTRUCBUS[18]; STRFIND = INSTRUCBUS[19];
  //   intr3__0[3:0] = intr; FETCH = PHASEFFBUS[0]; ADDR = PHASEFFBUS[1]; EXEC = PHASEFFBUS[2]; INTR_t = PHASEFFBUS[3];
  //   PSWSTART = PSW[0]; PSWZ = PSW[1]; PSWN = PSW[2]; PSWV = PSW[3]; PSWC = PSW[4]; PSWI = PSW[15]; rst = in_1

  // Notes on the sheet:
  //   Operaciona jedinica
  //   Upravljacka jedinica
endmodule

module RAM (
  input  [15:0] in_1,
  input  in_2,
  input  [7:0] in_3,
  input  in_4,
  input  in_5,
  input  in_6,
  output [7:0] out_7,
  output out_8
);

  wire and_1_out, and_2_out, CNT0, LDCNT, not_1_out, notCNT0, or_1_out, reg4_ld_sl_sr_1_p6, rsff_2_p4,
       rsff_2_p5, rsff_3_p4, sl;
  wire [3:0] CNT, LFSR;

  // RSFF rsff_1: pin names not known; wires that end beside it: 1'b0, in_2, in_6, sl
  or or_1 (or_1_out, in_4, in_5);
  // REG4_LD_SL_SR reg4_ld_sl_sr_1: pin names not known; wires that end beside it: 1'b0, 1'b0, in_2, 4'b1111, LFSR, reg4_ld_sl_sr_1_p6, sl, in_6
  // RisingEdge risingedge_1: pin names not known; wires that end beside it: or_1_out, in_2, LDCNT
  // MEM64Kx8 mem64kx8_1: pin names not known; wires that end beside it: in_1, 1'b1, in_2, in_3, out_7, in_4
  xor xor_1 (reg4_ld_sl_sr_1_p6, LFSR[2], LFSR[3]);
  and and_1 (and_1_out, CNT0, not_1_out);
  not not_1 (not_1_out, LDCNT);
  // RSFF rsff_2: pin names not known; wires that end beside it: and_1_out, in_2, LDCNT, rsff_2_p4, rsff_2_p5
  not not_2 (rsff_2_p4, in_6);
  and and_2 (and_2_out, rsff_2_p5, CNT0);
  // REG4m_DEC_LD reg4m_dec_ld_1: pin names not known; wires that end beside it: in_2, LFSR, CNT, LDCNT, notCNT0, notCNT0
  or or_2 (notCNT0, CNT[0], CNT[1], CNT[2], CNT[3]);
  // RSFF rsff_3: pin names not known; wires that end beside it: out_8, in_2, and_2_out, rsff_3_p4, out_8
  not not_3 (rsff_3_p4, in_6);
  not not_4 (CNT0, notCNT0);

  // Other names for the same wires on the sheet: ADR[15:0] = in_1; CLK = in_2; DIN[7:0] = in_3; DOUT[7:0] = out_7;
  //   fc = out_8; RDMEM = in_5; rst = in_6; WRMEM = in_4

  // Notes on the sheet:
  //   Random broj predstavlja vreme pristupa memoriji
  //   Brojac za generisanje random broja 
  //   Jedinica za generisanje function complete (fc) signala
  //   Brojac za dekrementiranje random broja
endmodule
